# Fritzing sketch Spider (saved by Fritzing 0.9.4)

parts:
  Q1 = NPN-Transistor [package="TO92 [THT]"]
  Q2 = NPN-Transistor [package="TO92 [THT]"]
  Q3 = NPN-Transistor [package="TO92 [THT]"]
  R1 = Resistor [tolerance=±5% resistance=220 package=THT]
  R2 = Resistor [tolerance=±5% resistance=220 package=THT]
  R3 = Resistor [tolerance=±5% resistance=220 package=THT]
  Part1 = Adafruit Stereo 3W Speaker Bonnet [part_number="Adafruit #"]
  MCU1 = Raspberry Pi Zero
  LED1 = RGB LED (com. cathode, rbg) [package="5 mm [THT]"]
  LED2 = RGB LED (com. cathode, rbg) [package="5 mm [THT]"]
  LED3 = RGB LED (com. cathode, rbg) [package="5 mm [THT]"]
  LED4 = RGB LED (com. cathode, rbg) [package="5 mm [THT]"]
  LED5 = RGB LED (com. cathode, rbg) [package="5 mm [THT]"]
  LED6 = RGB LED (com. cathode, rbg) [package="5 mm [THT]"]
  LED7 = RGB LED (com. cathode, rbg) [package="5 mm [THT]"]
  LED8 = RGB LED (com. cathode, rbg) [package="5 mm [THT]"]
  LED9 = smd LED [color="White (4500K)" package="0805 [SMD]"]
  LED10 = smd LED [color="White (4500K)" package="0805 [SMD]"]
  LED11 = smd LED [color="White (4500K)" package="0805 [SMD]"]
  PIR = PIR sensor
  SPKR1 = Loudspeaker
  SPKR2 = Loudspeaker
  JP1 = USB_MICROB_PLUG [package=micro-b-ra-smt]

nets (from the schematic view):
  N1: Q1.E, LED1.red_anode, LED2.red_anode, LED3.red_anode, LED4.red_anode, LED5.red_anode, LED6.red_anode, LED7.red_anode, LED8.red_anode
  N2: Q1.B, R1.Pin_1
  N3: Q1.C, Q2.C, Q3.C, MCU1.pin_2, MCU1.pin_4, PIR.VDD
  N4: Q2.E, LED1.green_anode, LED2.green_anode, LED3.green_anode, LED4.green_anode, LED5.green_anode, LED6.green_anode, LED7.green_anode, LED8.green_anode, LED9.anode, LED10.anode, LED11.anode
  N5: Q2.B, R2.Pin_1
  N6: Q3.E, LED1.blue_anode, LED2.blue_anode, LED3.blue_anode, LED4.blue_anode, LED5.blue_anode, LED6.blue_anode, LED7.blue_anode, LED8.blue_anode
  N7: Q3.B, R3.Pin_1
  N8: R1.Pin_0, MCU1.pin_37
  N9: R2.Pin_0, MCU1.pin_31
  N10: R3.Pin_0, MCU1.pin_33
  N11: Part1.RIGHT-, SPKR1.pin2
  N12: Part1.RIGHT+, SPKR1.pin1
  N13: Part1.LEFT+, SPKR2.pin1
  N14: Part1.LEFT-, SPKR2.pin2
  GND: MCU1.pin_6, MCU1.pin_20, MCU1.pin_39, LED1.common_cathode, LED2.common_cathode, LED3.common_cathode, LED4.common_cathode, LED5.common_cathode, LED6.common_cathode, LED7.common_cathode, LED8.common_cathode, LED9.cathode, LED10.cathode, LED11.cathode, PIR.GND, JP1.GND
  N15: MCU1.pin_32, PIR.SIG
  5V: JP1.VCC

notes:
  RED
  GREEN
  BLUE
  EYE 1
  EYE 2
  STRING OF 12 MINI WHITE LEDS
  Spider
  Ron Grimes
  github/rongrimes
  May 2020
  Board centre connector
  (line with red stripe)

custom parts:
  Adafruit Stereo 3W Speaker Bonnet: Hey Mr. DJ! Turn up that Raspberry Pi mix to the max with this cute 3W Stereo Amplifier Bonnet for Raspberry Pi. (It's not big enough to be an official HAT, so we called it a bonnet, you see?) It's the exact same size as a Raspberry Pi Zero but works with any and all Raspberry Pi computers with a 2x20 connector - A+, B+, Zero, Pi 2, Pi 3, etc. This Bonnet uses I2S a digital sound standard, so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
